// Logisim project lockwise_completo.circ as structural Verilog: 1 circuit, main circuit LOCKWISE
module LOCKWISE (
  input  S3,
  input  S2,
  input  S1,
  input  S0,
  input  CONFIRMA,
  input  TIMEOUT,
  input  RESET,
  input  CLK,
  output AGUARDANDO,
  output VERIFICANDO,
  output TRAVA_ABERTA,
  output BLOQUEADO,
  output SENHA_OK,
  output ERROS_C1,
  output ERROS_C0
);

  wire A1, A2, A3, B1, B2, C0N, C1N, CE, CLR, CLRN, D0, D1, DC0, DC1, E, EBAR, ECNT, EN, ERR, G, IE, IN, NE,
       P1, P2, Q0, Q0N, Q1, Q1N, RN, S2N, TN, X0, X1;

  not not_1 (S2N, S2);
  and and_1 (P1, S3, S2N);
  and and_2 (P2, S1, S0);
  and and_3 (AGUARDANDO, Q1N, Q0N);
  and and_4 (VERIFICANDO, Q1N, Q0);
  and and_5 (TRAVA_ABERTA, Q1, Q0N);
  and and_6 (BLOQUEADO, Q1, Q0);
  not not_2 (TN, TIMEOUT);
  not not_3 (RN, RESET);
  and and_7 (A1, Q1N, Q0, IE);
  and and_8 (A2, Q1, Q0N, TN);
  and and_9 (A3, Q1, Q0, RN);
  and and_10 (B1, Q1N, Q0N, CONFIRMA);
  and and_11 (B2, Q1N, Q0, NE);
  and and_12 (ECNT, ERROS_C1, ERROS_C0);
  not not_4 (EBAR, ECNT);
  or or_1 (CLR, TRAVA_ABERTA, RESET);
  and and_13 (EN, ERR, EBAR);
  // XOR_Gate xor_1: pin names not known; wires that end beside it: ERROS_C0, EN, X0
  and and_14 (G, ERROS_C0, EN);
  // XOR_Gate xor_2: pin names not known; wires that end beside it: ERROS_C1, G, X1
  and and_15 (SENHA_OK, P1, P2);
  and and_16 (ERR, VERIFICANDO, IN);
  or or_2 (CE, ERROS_C0, ERR);
  or or_3 (IE, SENHA_OK, E);
  and and_17 (NE, IN, E);
  or or_4 (D1, A1, A2, A3);
  or or_5 (D0, B1, B2, A3);
  not not_5 (CLRN, CLR);
  and and_18 (DC0, X0, CLRN);
  and and_19 (DC1, X1, CLRN);
  not not_6 (IN, SENHA_OK);
  D_Flip_Flop FF1 (.D(D1), .clk(CLK), .Q(Q1), .Qn(Q1N));  // open: preset, reset
  D_Flip_Flop FF0 (.D(D0), .clk(CLK), .Q(Q0), .Qn(Q0N));  // open: preset, reset
  D_Flip_Flop FFC1 (.D(DC1), .clk(CLK), .Q(ERROS_C1), .Qn(C1N));  // open: preset, reset
  D_Flip_Flop FFC0 (.D(DC0), .clk(CLK), .Q(ERROS_C0), .Qn(C0N));  // open: preset, reset
  and and_20 (E, ERROS_C1, CE);

  // Other names for the same wires on the sheet: AG = AGUARDANDO; BLQ = BLOQUEADO; C = CONFIRMA; C0 = ERROS_C0;
  //   C1 = ERROS_C1; IGUAL = SENHA_OK; LIB = TRAVA_ABERTA; R = RESET; T = TIMEOUT; VER = VERIFICANDO
endmodule
